// Logisim project cpu.circ as structural Verilog
module Timer (
  input  [1:0] TxCTR,
  input  in_2,
  input  CMP,
  input  [15:0] TxCR,
  input  in_5
);

  wire and_1_out, counter_1_carry, nor_1_out, nor_2_out, not_1_out, or_1_out, or_2_out, t_ff_1_qn, undriven,
       undriven_2;

  not not_1 (not_1_out, TxCTR[0]);
  and and_1 (and_1_out, not_1_out, CMP);
  or or_1 (or_1_out, TxCTR[0], TxCTR[1]);
  nor nor_1 (nor_1_out, undriven, nor_2_out);
  nor nor_2 (nor_2_out, nor_1_out, undriven_2);
  T_Flip_Flop t_ff_1 (.T(or_2_out), .clk(in_2), .Qn(t_ff_1_qn));  // open: Q, reset, preset
  or or_2 (or_2_out, CMP, counter_1_carry);
  Counter #(.max('h7), .width(3)) counter_1 (
    .clr(and_1_out), .load(1'b0), .up(or_1_out), .count(t_ff_1_qn), .clk(in_2), .carry(counter_1_carry));  // open: D, Q

  // Notes on the sheet:
  //   R
  //   S
  //   Q
  //   Q'
endmodule
